# Fritzing sketch TSFRL_master_module (saved by Fritzing 0.9.0b)

parts:
  IC1 = Voltage Regulator [package=to220-igo]
  U1 = MAX485 [package=dil08]
  C1 = Capacitor Polarized [package=cpol-radial-100uf-25v]
  C2 = Capacitor Polarized [package=cpol-radial-10uf-25v]
  R1 = Resistor [tolerance=±5% resistance=220 package=THT]
  POWER = LED - 3mm [color="Red (633nm)" package="3 mm [THT]"]
  J1 = rounded female pin header, 8 pins [form="♀ (female rounded)"]
  IC2 = Hex Inverter Schmitt Trigger SN74HC14 [package="DIP (Dual Inline)"]
  J2 = male pin header, 5 pins [form="♂ (male)"]
  TEST = LED - 3mm [color="Blue (525nm)" current=20pA package="3 mm [THT]"]
  DATA = LED - 3mm [color="Yellow (595nm)" package="3 mm [THT]"]
  ERR = LED - 3mm [color="Red (633nm)" package="3 mm [THT]"]
  DONE = LED - 3mm [color="Green (570nm)" package="3 mm [THT]"]
  Part1 = Arduino Nano (Rev3.0)
  J3 = male pin header, 2 pins [form="♂ (male)"]
  R2 = Resistor [tolerance=±5% resistance=220 package=THT]
  R3 = Resistor [tolerance=±5% resistance=220 package=THT]
  R4 = Resistor [tolerance=±5% resistance=220 package=THT]
  R5 = Resistor [tolerance=±5% resistance=220 package=THT]

nets:
  GND: IC1.GND, U1.GND, C1.-, C2.-, POWER.cathode, J1.pin1, IC2.GND, J2.pin2, TEST.cathode, DATA.cathode, Part1.GND
  12V: IC1.IN, C1.+
  N1: IC1.OUT, C2.+, R1.Pin_0
  N2: U1.RO, Part1.D12/MISO
  N3: U1.RE, U1.DE, Part1.D13/SCK, R2.Pin_0
  N4: U1.DI, Part1.D11/MOSI
  N5: U1.A, J2.pin3
  N6: U1.B, J2.pin4
  5V: U1.VCC, R1.Pin_1, POWER.anode, J1.pin8, IC2.VCC, J2.pin1, Part1.5V
  N7: J1.pin2, J2.pin5, Part1.RESET
  N8: J1.pin3, IC2.3A
  N9: J1.pin4, IC2.2A
  N10: J1.pin5, IC2.1A
  N11: J1.pin6, IC2.4A
  N12: J1.pin7, IC2.5A
  N13: IC2.1Y, Part1.D5
  N14: IC2.2Y, Part1.D4
  N15: IC2.3Y, Part1.D3
  N16: IC2.4Y, Part1.D6
  N17: IC2.5Y, Part1.D7
  N18: TEST.anode, R5.Pin_1
  N19: DATA.anode, R2.Pin_1
  N20: ERR.anode, R3.Pin_1
  N21: DONE.anode, R4.Pin_1
  N22: Part1.D8, R5.Pin_0
  N23: Part1.D9, R4.Pin_0
  N24: Part1.D10, R3.Pin_0
  N25: Part1.A5, J3.pin1
  N26: Part1.A4, J3.pin2

notes:
  TSFRL_master_module_keys
  8) +5v
  7) keyUP
  6) keyRIGHT
  5) keyLEFT
  4) keyDOWN
  3)keySTART
  2)keySTOP/CANCEL
  1)GND
